// Logisim project p2.circ as structural Verilog: 6 circuits, main circuit main
module main (
  input  in_1,
  input  in_2,
  input  in_3,
  input  in_4,
  input  in_5,
  input  in_6,
  input  in_7,
  input  in_8,
  input  in_9
);

  wire and_1_out, and_2_out, and_3_out, and_4_out, nand_1_out, nand_2_out, nand_3_out, nor_1_out, nor_2_out,
       nor_3_out, nor_4_out, not_1_out, not_2_out, not_3_out, not_4_out, not_5_out, not_6_out, or_1_out,
       or_2_out, or_3_out, xor_1_out;

  not not_1 (not_1_out, in_5);
  and and_1 (and_1_out, in_4, in_5);
  and and_2 (and_2_out, in_4, not_1_out);
  nor nor_1 (nor_1_out, in_8, in_9);
  or or_1 (or_1_out, in_6, in_7);
  nand nand_1 (nand_1_out, in_6, in_7);
  nor nor_2 (nor_2_out, in_1, in_2);
  nor nor_3 (nor_3_out, in_2, in_3);
  or or_2 (or_2_out, and_1_out, and_2_out);
  not not_2 (not_2_out, or_2_out);
  not not_3 (not_3_out, in_5);
  xor xor_1 (xor_1_out, nor_1_out, or_1_out);
  nand nand_2 (nand_2_out, nand_1_out, in_8);
  not not_4 (not_4_out, nor_2_out);
  not not_5 (not_5_out, nor_3_out);
  nand nand_3 (nand_3_out, not_2_out, not_3_out);
  and and_3 (and_3_out, xor_1_out, nand_2_out);
  and and_4 (and_4_out, in_7, not_6_out);
  not not_6 (not_6_out, in_9);
  nor nor_4 (nor_4_out, not_4_out, not_5_out);
  or or_3 (or_3_out, and_3_out, and_4_out);
endmodule

module Ej6Inversor3bits (
  input  in_1,
  input  in_2,
  input  in_3,
  input  in_4,
  output out_5,
  output out_6,
  output out_7
);

  wire and_1_out, and_2_out, and_3_out, and_4_out, and_5_out, and_6_out, not_1_out, not_2_out, not_3_out,
       not_4_out, not_5_out, not_6_out;

  not not_1 (not_1_out, in_1);
  not not_2 (not_2_out, in_2);
  not not_3 (not_3_out, in_1);
  not not_4 (not_4_out, in_3);
  not not_5 (not_5_out, in_1);
  not not_6 (not_6_out, in_4);
  and and_1 (and_1_out, in_2, not_1_out);
  and and_2 (and_2_out, in_1, not_2_out);
  and and_3 (and_3_out, in_3, not_3_out);
  and and_4 (and_4_out, in_1, not_4_out);
  and and_5 (and_5_out, in_4, not_5_out);
  and and_6 (and_6_out, in_1, not_6_out);
  or or_1 (out_5, and_1_out, and_2_out);
  or or_2 (out_6, and_3_out, and_4_out);
  or or_3 (out_7, and_5_out, and_6_out);
endmodule

module Ej7Inversor4bits (
  input  in_1,
  input  [3:0] in_2,
  input  [3:0] in_3,
  input  [3:0] in_4,
  output [3:0] out_5,
  output [3:0] out_6,
  output out_7
);

  wire and_1_out, and_2_out, and_3_out, and_4_out, and_5_out, and_6_out, and_7_out, and_8_out, not_1_out,
       not_2_out, not_3_out, not_4_out, not_5_out, not_6_out, not_7_out, not_8_out;

  not not_1 (not_1_out, in_1);
  not not_2 (not_2_out, in_2[0]);
  not not_3 (not_3_out, in_1);
  not not_4 (not_4_out, in_2[1]);
  not not_5 (not_5_out, in_1);
  not not_6 (not_6_out, in_2[2]);
  not not_7 (not_7_out, in_1);
  not not_8 (not_8_out, in_2[3]);
  and and_1 (and_1_out, in_2[0], not_1_out);
  and and_2 (and_2_out, in_1, not_2_out);
  and and_3 (and_3_out, in_2[1], not_3_out);
  and and_4 (and_4_out, in_1, not_4_out);
  and and_5 (and_5_out, in_2[2], not_5_out);
  and and_6 (and_6_out, in_1, not_6_out);
  and and_7 (and_7_out, in_2[3], not_7_out);
  and and_8 (and_8_out, in_1, not_8_out);
  or or_1 (out_5[0], and_1_out, and_2_out);
  or or_2 (out_5[1], and_3_out, and_4_out);
  or or_3 (out_5[2], and_5_out, and_6_out);
  or or_4 (out_5[3], and_7_out, and_8_out);
  sumador4Bits sumador4bits_1 (.A(in_3), .B(in_4), .S(out_6), .Cout(out_7));  // open: Cin
endmodule

module SumadorSimple (
  input  A,
  input  B,
  output C,
  output out_4
);

  and and_1 (C, B, A);
  xor xor_1 (out_4, A, B);

  // Notes on the sheet:
  //   S
endmodule

module SumadorCompleto (
  input  A,
  input  B,
  input  Cin,
  output S,
  output Cout
);

  wire and_1_out, and_2_out, xor_1_out;

  and and_1 (and_1_out, B, A);
  xor xor_1 (xor_1_out, A, B);
  and and_2 (and_2_out, Cin, xor_1_out);
  xor xor_2 (S, xor_1_out, Cin);
  or or_1 (Cout, and_2_out, and_1_out);
endmodule

module sumador4Bits (
  input  [3:0] A,
  input  Cin,
  input  [3:0] B,
  output [3:0] S,
  output Cout
);

  wire sumadorcompleto_1_cout, sumadorcompleto_2_cout, sumadorcompleto_3_cout;

  SumadorCompleto sumadorcompleto_1 (.A(A[0]), .B(B[0]), .Cin(Cin), .S(S[0]), .Cout(sumadorcompleto_1_cout));
  SumadorCompleto sumadorcompleto_2 (
    .A(A[1]), .B(B[1]), .Cin(sumadorcompleto_1_cout), .S(S[1]), .Cout(sumadorcompleto_2_cout));
  SumadorCompleto sumadorcompleto_3 (
    .A(A[2]), .B(B[2]), .Cin(sumadorcompleto_2_cout), .S(S[2]), .Cout(sumadorcompleto_3_cout));
  SumadorCompleto sumadorcompleto_4 (.A(A[3]), .B(B[3]), .Cin(sumadorcompleto_3_cout), .S(S[3]), .Cout(Cout));
  Hex_Digit_Display hex_digit_display_1 (.value(S));  // open: dp
endmodule
